# Fritzing sketch HelloLED (saved by Fritzing 0.9.3b)
breadboards: 1

parts:
  Part1 = Arduino Mega ADK (Rev3)
  LED2 = smd LED [color="Red (633nm)" package="0805 [SMD]"]
  R1 = Resistor [tolerance=±5% resistance=220 package="0805 [SMD]"]

nets:
  N1: Part1.GND, LED2.cathode
  N2: Part1.D1/TX0, R1.Pin_1
  N3: LED2.anode, R1.Pin_0
