# Fritzing sketch HelloInput (saved by Fritzing 0.9.3b)
breadboards: 1

parts:
  Part1 = Arduino Mega ADK (Rev3)
  R1 = Resistor [tolerance=±5% resistance=220 package="0805 [SMD]"]
  LED1 = smd LED [color="Red (633nm)" package="0805 [SMD]"]
  S1 = Pushbutton [package="[SMD]"]

nets:
  N1: Part1.D8_PWM, LED1.anode
  N2: Part1.5V, S1.Pin_3, S1.Pin_4
  N3: Part1.D2_PWM, R1.Pin_0, S1.Pin_1, S1.Pin_2
  N4: Part1.GND, R1.Pin_1, LED1.cathode
