# Fritzing sketch HelloDisplay (saved by Fritzing 0.9.3b)

parts:
  Part1 = Arduino Mega ADK (Rev3)
  U2 = LCD-16X2 [package=lcd-16x2_nosilk]

nets:
  N1: Part1.GND, U2.DB1
  N2: Part1.D10_PWM, U2.E
  N3: Part1.D9_PWM, U2.RS
  N4: Part1.5V, U2.DB3
  N5: Part1.D2_PWM, U2.VDD
